# Fritzing sketch DC Antenna Rotor Controller (saved by Fritzing 0.9.4)
breadboards: 1

parts:
  R1 = Resistor [tolerance=±5% resistance=220 package=THT]
  R2 = Resistor [tolerance=±5% resistance=220 package=THT]
  R12 = Resistor [tolerance=±5% resistance=220 package=THT]
  LED3 = LED - 5mm [color="Red (633nm)" package="5 mm [THT]"]
  Q2 = Basic FET N-Channel [package="TO220 [THT]"]
  Q3 = Basic FET N-Channel [package="TO220 [THT]"]
  D2 = Rectifier Diode [part_number=1N4001 package="300 mil [THT]"]
  D4 = Rectifier Diode [part_number=1N4001 package="300 mil [THT]"]
  DS2Y-5-DC5V3 = DS2Y-5-DC5V [part_number=DS2Y-5-DC5V]
  R13 = Resistor [tolerance=±5% resistance=220 package=THT]
  R14 = Resistor [tolerance=±5% resistance=220 package=THT]
  R15 = Resistor [tolerance=±5% resistance=220 package=THT]
  R16 = Resistor [tolerance=±5% resistance=220 package=THT]
  R17 = Resistor [tolerance=±5% resistance=220 package=THT]
  Q4 = Basic FET N-Channel [package="TO220 [THT]"]
  D5 = Rectifier Diode [part_number=1N4001 package="300 mil [THT]"]
  DS2Y-5-DC5V4 = DS2Y-5-DC5V [part_number=DS2Y-5-DC5V]
  R18 = Resistor [tolerance=±5% resistance=220 package=THT]
  R19 = Resistor [tolerance=±5% resistance=220 package=THT]
  R20 = Resistor [tolerance=±5% resistance=220 package=THT]
  LED5 = LED - 5mm [color="Red (633nm)" package="5 mm [THT]"]
  Q5 = Basic FET N-Channel [package="TO220 [THT]"]
  D6 = Rectifier Diode [part_number=1N4001 package="300 mil [THT]"]
  DS2Y-5-DC5V5 = DS2Y-5-DC5V [part_number=DS2Y-5-DC5V]
  U1 = Voltage Regulator - 5V [package="TO220 [THT]"]
  C1 = Electrolytic Capacitor [capacitance=1µF package="100 mil [THT, electrolytic]"]
  C2 = Electrolytic Capacitor [capacitance=1µF package="100 mil [THT, electrolytic]"]
  LED6 = LED - 5mm [color="Red (633nm)" package="5 mm [THT]"]

nets:
  GND: R1.Pin_0, Q2.source, Q3.source, D4.anode, R13.Pin_0, R16.Pin_0, Q4.source, R19.Pin_0, Q5.source, U1.GND, C1.-, C2.-
  Vdirection: R1.Pin_1, R2.Pin_0, Q3.gate
  5V: R2.Pin_1, R14.Pin_1, R17.Pin_1, R20.Pin_1, U1.output_voltage, C2.+
  N1: R12.Pin_0, LED3.anode
  12V: R12.Pin_1, D2.cathode, DS2Y-5-DC5V3.1_+, R15.Pin_1, D5.cathode, DS2Y-5-DC5V4.1_+, R18.Pin_1, D6.cathode, DS2Y-5-DC5V5.1_+, U1.input_voltage, C1.+
  N2: LED3.cathode, Q3.drain, D2.anode, DS2Y-5-DC5V3.16_-
  Vpwm: Q2.gate, R13.Pin_1, R14.Pin_0
  N3: Q2.drain, DS2Y-5-DC5V3.6_N.C., DS2Y-5-DC5V3.9_N.O.
  N4: D4.cathode, DS2Y-5-DC5V3.8_N.O., DS2Y-5-DC5V3.11_N.C., DS2Y-5-DC5V4.9_N.O.
  Motor B: DS2Y-5-DC5V3.4_COM
  Motor A: DS2Y-5-DC5V3.13_COM
  N5: R15.Pin_0, LED6.anode
  Venable: R16.Pin_1, R17.Pin_0, Q4.gate
  N6: Q4.drain, D5.anode, DS2Y-5-DC5V4.16_-, LED6.cathode
  N7: DS2Y-5-DC5V4.13_COM, DS2Y-5-DC5V5.4_COM
  N8: R18.Pin_0, LED5.anode
  Vdrive: R19.Pin_1, R20.Pin_0, Q5.gate
  N9: LED5.cathode, Q5.drain, D6.anode, DS2Y-5-DC5V5.16_-
  48V: DS2Y-5-DC5V5.8_N.O.
  6V: DS2Y-5-DC5V5.6_N.C.
